# Fritzing sketch WWWIII-FINAL (saved by Fritzing 0.9.3b)
breadboards: 2

parts:
  Part1 = sparkfun-battery-babysitter  # not connected
  U1 = atmega328 [package=dip]
  Part2 = Adafruit HUZZAH32 ESP32 Feather [part_number="Adafruit #3405"]
  C1 = Electrolytic Capacitor [capacitance=1µF package="200 mil [THT, electrolytic]"]  # not connected
  C2 = Electrolytic Capacitor [capacitance=1µF package="200 mil [THT, electrolytic]"]
  R1 = Resistor [tolerance=±5% resistance=10k package=THT]
  R2 = Resistor [tolerance=±5% resistance=10k package=THT]
  S1 = Pushbutton [package=THT]
  LED1 = LED - 5mm [color="Red (633nm)" package="5 mm [THT]"]
  LED2 = LED - 5mm [color="Red (633nm)" package="5 mm [THT]"]
  LED3 = LED - 5mm [color="Red (633nm)" package="5 mm [THT]"]
  R3 = Resistor [tolerance=±5% resistance=100 package=THT]
  R4 = Resistor [tolerance=±5% resistance=100 package=THT]
  R5 = Resistor [tolerance=±5% resistance=100 package=THT]

nets:
  N1: U1.RESET, R2.Pin_1, S1.leg0
  N2: U1.D3_(PWM), Part2.EN, R1.Pin_1
  N3: U1.VCC, U1.AVCC, Part2.VBAT, C2.+, R2.Pin_0
  GND: U1.GND, Part2.GND, C2.-, R1.Pin_0, S1.leg1, R3.Pin_0, R4.Pin_0, R5.Pin_0
  N4: U1.D11_(PWM), LED3.anode
  N5: U1.D12, LED2.anode
  N6: U1.D13, LED1.anode
  N7: LED1.cathode, R3.Pin_1
  N8: LED2.cathode, R4.Pin_1
  N9: LED3.cathode, R5.Pin_1

notes:
  - Solar Panel +
  switch
