# Fritzing sketch WWWIII (saved by Fritzing 0.9.3b)
breadboards: 2

parts:
  U1 = atmega328 [package=dip]
  Part1 = Adafruit HUZZAH32 ESP32 Feather [part_number="Adafruit #3405"]
  Part2 = sparkfun-battery-babysitter
  Part3 = Lithium Ion Polymer Battery 3.7v 1200mAh [part_number=258]

nets:
  N1: U1.VCC, U1.AVCC, Part1.VBAT, Part2.OUT, Part2.V_PU
  GND: U1.GND, Part1.GND, Part2.GND, Part3.negative
  N2: U1.A4, Part2.SCL
  N3: U1.A5, Part2.SDA
  N4: Part2.BATTERY_IN, Part3.positive

custom parts:
  Lithium Ion Polymer Battery 3.7v 1200mAh: Lithium ion polymer (also known as 'lipo' or 'lipoly') batteries are thin, light and powerful. The output ranges from 4.2V when completely charged to 3.7V. This battery has a capacity of 1200mAh for a total of about 4.5 Wh. The batteries come pre-attached with a genuine 2-pin JST-PH connector as shown and include the necessary protection circuitry.
